# Fritzing sketch 1 (saved by Fritzing 0.8.7b)
circuit board: 8.46667cm x 5.64444cm
breadboards: 1

parts:
  U1 = RELAY-SOLIDSTATE [package=relay-s108t02]
  U2 = RELAY-2 [package=relay-g5v]
  U3 = RELAY-2 [package=relay-g5v]
  V1 = DC Motor
  V12 = DC Power [voltage=12V]
  U4 = RELAY-2 [package=relay-g5v]
  U5 = RELAY-2 [package=relay-g5v]
  V2 = DC Motor
  V13 = DC Power [voltage=12V]
  U6 = RELAY-2 [package=relay-g5v]
  U7 = RELAY-2 [package=relay-g5v]
  V4 = DC Motor
  V5 = DC Power [voltage=12V]
  U8 = RELAY-2 [package=relay-g5v]
  U9 = RELAY-2 [package=relay-g5v]
  V7 = DC Motor
  V8 = DC Power [voltage=12V]
  U10 = RELAY-2 [package=relay-g5v]
  U11 = RELAY-2 [package=relay-g5v]
  V10 = DC Motor
  V11 = DC Power [voltage=12V]
  Raspberry_Pi_1 = Raspberry Pi 3
  P1 = DC Motor
  P2 = DC Motor
  U12 = RELAY-SOLIDSTATE [package=relay-s108t02]
  V3 = AC Power [voltage=230 frequency=60]
  HL1 = PHOTOCELL [package=photocell-kit]
  HL2 = PHOTOCELL [package=photocell-kit]
  HL3 = PHOTOCELL [package=photocell-kit]
  LL1 = PHOTOCELL [package=photocell-kit]
  LL2 = PHOTOCELL [package=photocell-kit]
  R1 = Resistor [tolerance=±5% resistance=10k package=THT]
  R2 = Resistor [tolerance=±5% resistance=10k package=THT]
  R3 = Resistor [tolerance=±5% resistance=10k package=THT]
  R4 = Resistor [tolerance=±5% resistance=10k package=THT]
  R5 = Resistor [tolerance=±5% resistance=10k package=THT]
  Part1 = Photon
  JP1 = Header 2 [package=springterminal-2.54mm-2]
  U13 = RELAY-SOLIDSTATE [package=relay-s108t02]
  T1 = Temperature Sensor (Thermistor) [thermistor_type=PTC package=THT]
  T2 = Temperature Sensor (Thermistor) [thermistor_type=PTC package=THT]
  T3 = Temperature Sensor (Thermistor) [thermistor_type=PTC package=THT]
  H1 = Inductor [package="0603 [SMD]"]
  H3 = Inductor [package="0603 [SMD]"]
  JP5 = Header 2 [package=springterminal-2.54mm-2]
  JP6 = Header 2 [package=springterminal-2.54mm-2]  # not connected
  JP7 = Header 2 [package=springterminal-2.54mm-2]
  JP8 = Header 2 [package=springterminal-2.54mm-2]
  JP9 = Header 2 [package=springterminal-2.54mm-2]
  JP10 = Header 2 [package=springterminal-2.54mm-2]
  V14 = DC Power [voltage=5V]
  U14 = RELAY-SOLIDSTATE [package=relay-s108t02]
  V15 = AC Power [voltage=230 frequency=60]

nets:
  N1: U1.T1, U12.T1, V3.V+
  N2: U1.T2, P1.pin_1
  N3: U1.+, Raspberry_Pi_1.GIPO6
  N4: U2.1, U3.10, V12.V+
  N5: U2.2, U3.2, U4.2, U5.2, U6.2, U7.2, U8.2, U9.2, U10.2, U11.2
  N6: U2.5, V1.pin_1
  N7: U2.9, Raspberry_Pi_1.GPIO3
  N8: U2.10, U3.1, V12.V-
  N9: U3.6, V1.pin_2
  N10: U3.9, Raspberry_Pi_1.GPIO2
  N11: U4.1, U5.10, V13.V+
  N12: U4.5, V2.pin_1
  N13: U4.9, Raspberry_Pi_1.GIPO17
  N14: U5.1, V13.V-
  N15: U5.6, V2.pin_2
  N16: U5.9, Raspberry_Pi_1.GIPO4
  N17: U6.1, V5.V-
  N18: U6.6, V4.pin_2
  N19: U6.9, Raspberry_Pi_1.GIPO10
  N20: U6.10, U7.1, V5.V+
  N21: U7.5, V4.pin_1
  N22: U7.9, Raspberry_Pi_1.GIPO9
  N23: U8.1, V8.V-
  N24: U8.6, V7.pin_2
  N25: U8.9, Raspberry_Pi_1.GIPO27
  N26: U8.10, U9.1, V8.V+
  N27: U9.5, V7.pin_1
  N28: U9.9, Raspberry_Pi_1.GIPO22
  N29: U10.6, V10.pin_2
  N30: U10.9, Raspberry_Pi_1.GIPO11
  N31: U10.10, U11.1, V11.V+
  N32: U11.5, V10.pin_1
  N33: U11.9, Raspberry_Pi_1.GIPO5
  3V3: Raspberry_Pi_1.3v3, Raspberry_Pi_1.3V3, Raspberry_Pi_1.GIPO15, Raspberry_Pi_1.GIPO14, HL1.P$1, HL2.P$1, HL3.P$1, LL1.P$1, LL2.P$1
  N34: Raspberry_Pi_1.GIPO13, U12.+
  N35: Raspberry_Pi_1.GIPO19, HL1.P$2, R1.Pin_0
  N36: Raspberry_Pi_1.GIPO26, HL2.P$2, R2.Pin_0
  N37: Raspberry_Pi_1.GND, R1.Pin_1, R2.Pin_1, R3.Pin_1, R4.Pin_1, R5.Pin_1
  N38: Raspberry_Pi_1.GIPO18, LL2.P$2, R5.Pin_0
  N39: P1.pin_2, P2.pin_2, V3.V-
  N40: P2.pin_1, U12.T2
  N41: HL3.P$2, R3.Pin_0
  N42: LL1.P$2, R4.Pin_0
  N43: Part1.A0, T1.pin_1, JP9.2
  N44: Part1.A1, T2.pin_1, JP8.2
  N45: Part1.A2, T3.pin_1, JP7.2
  N46: Part1.VIN, JP10.2, V14.V+
  N47: Part1.D0, JP1.1, U13.+
  N48: Part1.D1, JP5.1, U14.+
  N49: Part1.GND, JP1.2, U13.-, T1.pin_0, T2.pin_0, T3.pin_0, JP5.2, JP7.1, JP8.1, JP9.1, JP10.1, V14.V-, U14.-
  N50: U13.T1, H1.pin_1
  N51: U13.T2, U14.T2, V15.V-
  N52: H1.pin_0, H3.pin_0, V15.V+
  N53: H3.pin_1, U14.T1
